# Fritzing sketch SchemaElectrica (saved by Fritzing 0.9.3b)
breadboards: 1

parts:
  WeMos_D1_R1 = WeMos D1 R2
  Part1 = Arduino Uno (Rev3)
  M1 = DC Motor
  M2 = DC Motor
  M3 = DC Motor
  M4 = DC Motor
  hc-sr1 = hc-sr04
  hc-sr2 = hc-sr04
  hc-sr3 = hc-sr04
  hc-sr4 = hc-sr04
  S1 = H-Bridge with L298N
  S2 = H-Bridge with L298N
  U1 = TEMPERATURE-SENSOR [package=to-92]
  hc-sr5 = hc-sr04
  R1 = Resistor [tolerance=±5% resistance=220 package=THT]
  Part2 = Lilypad Power Supply

nets:
  N1: WeMos_D1_R1.D3, hc-sr4.Echo
  N2: WeMos_D1_R1.(D6), hc-sr4.Trig
  N3: WeMos_D1_R1.(D7), hc-sr3.Echo
  N4: WeMos_D1_R1.D8, hc-sr3.Trig
  N5: WeMos_D1_R1.D14, Part1.A4/SDA
  N6: WeMos_D1_R1.D15, Part1.A5/SCL
  VCC: WeMos_D1_R1.VIN, Part1.VIN, hc-sr1.VCC, hc-sr2.VCC, hc-sr3.VCC, hc-sr4.VCC, S1.12V, S2.12V, U1.VCC, hc-sr5.VCC, R1.Pin_1, Part2.+
  GND: WeMos_D1_R1.GND, Part1.GND, hc-sr1.GND, hc-sr2.GND, hc-sr3.GND, hc-sr4.GND, S1.GND, S2.GND, U1.GND, hc-sr5.GND, Part2.GND
  N7: Part1.A0, hc-sr2.Echo
  N8: Part1.A1, hc-sr2.Trig
  N9: Part1.A2, hc-sr1.Echo
  N10: Part1.A3, hc-sr1.Trig
  N11: Part1.D8, S1.IN3
  N12: Part1.D9_PWM, S1.IN2
  N13: Part1.D10_PWM/SS, S1.IN1
  N14: Part1.D11_PWM/MOSI, hc-sr5.Echo
  N15: Part1.D12/MISO, hc-sr5.Trig
  N16: Part1.D13/SCK, U1.ADJ, R1.Pin_0
  N17: Part1.D3_PWM, S2.IN4
  N18: Part1.D4, S2.IN3
  N19: Part1.D5_PWM, S2.IN2
  N20: Part1.D6_PWM, S2.IN1
  N21: Part1.D7, S1.IN4
  N22: M1.pin_1, S1.M1-02
  N23: M2.pin_1, S1.M2-02
  N24: M2.pin_2, S1.M2-01
  N25: M3.pin_1, S2.M1-02
  N26: M3.pin_2, S2.M1-01
  N27: M4.pin_1, S2.M2-02
  N28: M4.pin_2, S2.M2-01
  N29: S1.ENA, S1.ENA-5V
  N30: S1.ENB, S1.ENB-5V
  N31: S2.ENA, S2.ENA-5V
  N32: S2.ENB, S2.ENB-5V

custom parts:
  WeMos D1 R2: The D1 R2 is a mini wifi board based on the ESP-8266EX.
  H-Bridge with L298N: h-bridge
